// Logisim project cpu.circ as structural Verilog: 1 circuit, main circuit cpu
module cpu (
  input  clk,
  input  [31:0] INSTRUCTION,
  input  [31:0] READ_DATA,
  output [31:0] WRITE_ADDRESS,
  output [31:0] PROGRAM_COUNTER,
  output [31:0] ra,
  output [31:0] sp,
  output [31:0] t0,
  output [31:0] t1,
  output [31:0] t2,
  output [31:0] s0,
  output [31:0] s1,
  output [31:0] a0,
  output [31:0] tohost,
  output [3:0] WRITE_ENABLE,
  output [31:0] WRITE_DATA
);

  wire [31:0] adder_1_out, alu_1_result, imm_gen_1_imm, INSTRUCTION_2, multiplexer_1_out,
       regfile_1_read_data_1;

  Register #(.width(32)) PC (.D(adder_1_out), .clk(clk), .Q(PROGRAM_COUNTER));  // open: en, clr
  Adder #(.width(32)) adder_1 (.a(PROGRAM_COUNTER), .b(32'h4), .out(adder_1_out));  // open: cin, cout
  Register #(.width(32)) register_1 (.D(INSTRUCTION), .clk(clk), .Q(INSTRUCTION_2));  // open: en, clr
  // control_logic control_logic_1: pin names not known
  Multiplexer #(.enable("false"), .select(2), .width(32)) multiplexer_1 (
    .in0(alu_1_result), .out(multiplexer_1_out), .sel(2'b00));  // open: in1, in2, in3
  regfile regfile_1 (
    .rs1(INSTRUCTION_2[19:15]), .rd(INSTRUCTION_2[11:7]), .Write_Data(multiplexer_1_out), .RegWEn(1'b1),
    .clk(clk), .ra(ra), .sp(sp), .t0(t0), .t1(t1), .t2(t2), .s0(s0), .s1(s1), .a0(a0),
    .Read_Data_1(regfile_1_read_data_1));  // open: rs2, Read_Data_2
  // branch_comp branch_comp_1: pin names not known
  imm_gen imm_gen_1 (.inst(INSTRUCTION_2), .imm(imm_gen_1_imm));  // open: ImmSel
  alu alu_1 (.Result(alu_1_result), .A(regfile_1_read_data_1), .B(imm_gen_1_imm));  // open: ALUSel
  csr csr_1 (.tohost(tohost));  // open: CSR_address, CSR_din, CSR_WE, clk

  // Other names for the same wires on the sheet: rd[4:0] = INSTRUCTION_2[11:7]; rs1[4:0] = INSTRUCTION_2[19:15]

  // Notes on the sheet:
  //   Output to IMEM
  //   IMEM (do **NOT** move this)
  //   Inputs from IMEM
  //   It is OK to move the PC, RegFile, ALU, MEM, Branch Comp, Imm Gen, and Control Logic to wherever is most convenient for you when constructing your CPU, and to delete this text
  //   Inputs/Outputs for testing. Do **NOT** move these.
  //   Outputs To DMEM
  //   DMEM (do **NOT** move this)
  //   Inputs From DMEM
endmodule
